# Fritzing sketch schematics (saved by Fritzing 0.8.7b)
breadboards: 5

parts:
  Nano1 = Arduino Nano v2.3
  Nano2 = Arduino Nano v2.3
  Nano3 = Arduino Nano v2.3
  R1 = Resistor [tolerance=±5% resistance=1.5k package=THT]
  R2 = Resistor [tolerance=±5% resistance=1.5k package=THT]
  R3 = Resistor [tolerance=±1% resistance=1 package=THT]
  R4 = Resistor [tolerance=±1% resistance=1 package=THT]
  R5 = Resistor [tolerance=±1% resistance=1 package=THT]
  R6 = Resistor [tolerance=±1% resistance=1 package=THT]
  R7 = Resistor [tolerance=±1% resistance=1 package=THT]
  R8 = Resistor [tolerance=±1% resistance=1 package=THT]
  R9 = Resistor [tolerance=±1% resistance=1 package=THT]
  R10 = Resistor [tolerance=±1% resistance=1 package=THT]
  R11 = Resistor [tolerance=±1% resistance=1 package=THT]
  R12 = Resistor [tolerance=±1% resistance=1 package=THT]
  R13 = Resistor [tolerance=±1% resistance=1 package=THT]
  R14 = Resistor [tolerance=±1% resistance=1 package=THT]
  R15 = Resistor [tolerance=±1% resistance=1 package=THT]
  R16 = Resistor [tolerance=±1% resistance=1 package=THT]
  R17 = Resistor [tolerance=±1% resistance=1 package=THT]
  R18 = Resistor [tolerance=±1% resistance=1 package=THT]
  R19 = Resistor [tolerance=±1% resistance=1 package=THT]
  R20 = Resistor [tolerance=±1% resistance=1 package=THT]
  R21 = Resistor [tolerance=±1% resistance=1 package=THT]
  R22 = Resistor [tolerance=±1% resistance=1 package=THT]
  R23 = Resistor [tolerance=±1% resistance=1 package=THT]
  R24 = Resistor [tolerance=±1% resistance=1 package=THT]
  J1 = Basic Servo
  J2 = Basic Servo
  J3 = Basic Servo
  J4 = Basic Servo
  J5 = Basic Servo
  J6 = Basic Servo
  J7 = Basic Servo
  J8 = Basic Servo
  J9 = Basic Servo
  J10 = Basic Servo
  J11 = Basic Servo
  R25 = Rotary Potentiometer (Large) [maximum_resistance=100kΩ package=THT]
  R26 = Rotary Potentiometer (Large) [maximum_resistance=100kΩ package=THT]
  S1 = Tilt Switch [package=THT]
  S2 = Tilt Switch [package=THT]
  Arduino1 = Arduino Uno (Rev3)

nets:
  GND: Nano1.GND, Nano2.GND, Nano3.GND, Arduino1.GND
  N1: Nano1.D3, J8.pulse
  N2: Nano1.D4, J7.pulse
  N3: Nano1.D5, J6.pulse
  N4: Nano1.D6, J5.pulse
  N5: Nano1.A5, Nano2.A5, Nano3.A5
  N6: Nano1.A4, Nano2.A4, Nano3.A4
  N7: Nano1.A3, R12.Pin_1, R22.Pin_1, J5.gnd
  N8: Nano1.A2, R13.Pin_1, R23.Pin_1, J6.gnd
  N9: Nano1.A1, R21.Pin_1, R24.Pin_1, J7.gnd
  N10: Nano1.A0, R8.Pin_1, R17.Pin_1, J8.gnd
  +5V: Nano1.+5V, Nano2.+5V, Nano3.+5V, S2.Pin_2
  N11: Nano2.D3, J2.pulse
  N12: Nano2.D4, J3.pulse
  N13: Nano2.D5, J4.pulse
  N14: Nano2.D6, J1.pulse
  N15: Nano2.A3, R6.Pin_1, R16.Pin_1, J1.gnd
  N16: Nano2.A2, R7.Pin_1, R15.Pin_1, J4.gnd
  N17: Nano2.A1, R5.Pin_1, R14.Pin_1, J3.gnd
  N18: Nano2.A0, R3.Pin_1, R4.Pin_1, J2.gnd
  N19: Nano3.D3, J9.pulse
  N20: Nano3.D4, J10.pulse
  N21: Nano3.D5, J11.pulse
  N22: Nano3.A1, R10.Pin_1, R19.Pin_1, J10.gnd
  N23: Nano3.A0, R11.Pin_1, R20.Pin_1, J11.gnd
  N24: R1.Pin_0, R2.Pin_0, S1.Pin_1, S2.Pin_1
  N25: R3.Pin_0, R4.Pin_0, R5.Pin_0, R6.Pin_0, R7.Pin_0, R8.Pin_0, R9.Pin_0, R10.Pin_0, R11.Pin_0, R12.Pin_0, R13.Pin_0, R14.Pin_0, R15.Pin_0, R16.Pin_0, R17.Pin_0, R18.Pin_0, R19.Pin_0, R20.Pin_0, R21.Pin_0, R22.Pin_0, R23.Pin_0, R24.Pin_0, R26.leg2
  N26: R9.Pin_1, R18.Pin_1, J9.gnd
  VCC: J1.vcc, J2.vcc, J3.vcc, J4.vcc, J5.vcc, J6.vcc, J7.vcc, J8.vcc, J9.vcc, J10.vcc, J11.vcc, R26.leg1
  N27: R25.wiper, Arduino1.A0
  N28: R26.wiper, Arduino1.A1
